// Logisim project 2_Bit_Comparator.circ as structural Verilog: 1 circuit, main circuit main
module main (
  input  [1:0] A,
  input  [1:0] B
);

  wire and_1_out, and_2_out, and_3_out, and_4_out, and_5_out, and_6_out, EQ0_out, EQ1_out, EQ_out, GT0_out,
       GT1_out, GT_out, LT0_out, LT1_out, LT_out, not_1_out, not_2_out, not_3_out, not_4_out;

  not not_1 (not_1_out, A[1]);
  not not_2 (not_2_out, A[0]);
  not not_3 (not_3_out, B[1]);
  not not_4 (not_4_out, B[0]);
  and and_1 (and_1_out, A[1], B[1]);
  and and_2 (and_2_out, not_1_out, not_3_out);
  and and_3 (and_3_out, A[0], B[0]);
  and and_4 (and_4_out, not_2_out, not_4_out);
  and GT1 (GT1_out, A[1], not_3_out);
  and GT0 (GT0_out, A[0], not_4_out);
  and LT1 (LT1_out, not_1_out, B[1]);
  and LT0 (LT0_out, not_2_out, B[0]);
  or EQ1 (EQ1_out, and_1_out, and_2_out);
  or EQ0 (EQ0_out, and_3_out, and_4_out);
  and and_5 (and_5_out, EQ1_out, GT0_out);
  and and_6 (and_6_out, EQ1_out, LT0_out);
  and EQ (EQ_out, EQ1_out, EQ0_out);
  LED EQUAL (.in(EQ_out));
  or GT (GT_out, GT1_out, and_5_out);
  LED A_IS_GREATER (.in(GT_out));
  or LT (LT_out, LT1_out, and_6_out);
  LED A_IS_LESSER (.in(LT_out));
endmodule
